# Fritzing sketch Untitled Sketch 2 (saved by Fritzing 0.9.3b)

parts:
  Part1 = Arduino Uno (Rev3)
  LED1 = LED - 5mm [color="Red (633nm)" package="5 mm [THT]"]
  Part3 = FONA 800 Shield
  R1 = Resistor [tolerance=±5% resistance=220 package=THT]

nets:
  N1: Part1.D8, Part3.D8
  N2: Part1.D9_PWM, Part3.D9
  N3: Part1.D13/SCK, LED1.anode
  GND: Part1.GND, Part3.GND, R1.Pin_0
  N4: Part1.D0/RX, Part3.D0
  N5: Part1.D1/TX, Part3.D1
  N6: Part1.D2, Part3.D2
  N7: Part1.D3_PWM, Part3.D3
  N8: Part1.D4, Part3.D4
  N9: Part1.D5_PWM, Part3.D5
  N10: Part1.D6_PWM, Part3.D6
  N11: Part1.D7, Part3.D7
  N12: Part1.ioref, Part3.IOREF
  N13: Part1.RESET, Part3.RST
  N14: Part1.3V3, Part3.3V
  5V: Part1.5V, Part3.5V
  VIN: Part1.VIN, Part3.VIN
  N15: Part1.N/C, Part3.NC

custom parts:
  FONA 800 Shield: This shield fits on top of any classic Arduino or compatible, and packs a surprising amount of technology into it's little frame. At the heart is a GSM cellular module (we use the latest SIM800) the size of a postage stamp. Quad-band 850/900/1800/1900MHz - connect onto any global GSM network with any 2G SIM (in the USA, T-Mobile is suggested) Make and receive voice calls using a headset OR an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
